// Logisim project labo3.circ as structural Verilog: 6 circuits, main circuit main
module main (
);


  // Notes on the sheet:
  //   Attention, votre version de Logisim
  //   ne contient pas de tracker. Si vous
  //   enregistrez votre projet, toutes les
  //   informations du tracker seront
  //   définitivement effacées.
endmodule

module CUSTOM (
  input  [3:0] A,
  input  [3:0] B,
  input  in_3
);

  wire add1bit_1_c_out, add1bit_2_c_out, add1bit_3_c_out;
  wire [3:0] add1bit_1_d;

  ADD1BIT add1bit_1 (.A(A[0]), .B(A[1]), .D(add1bit_1_d[0]), .C_out(add1bit_1_c_out));  // open: C_in
  ADD1BIT add1bit_2 (.A(A[2]), .B(A[3]), .C_in(add1bit_1_c_out), .D(add1bit_1_d[1]), .C_out(add1bit_2_c_out));
  ADD1BIT add1bit_3 (.A(B[0]), .B(B[1]), .C_in(add1bit_2_c_out), .D(add1bit_1_d[2]), .C_out(add1bit_3_c_out));
  ADD1BIT add1bit_4 (.A(B[2]), .B(B[3]), .C_in(add1bit_3_c_out), .D(add1bit_1_d[3]));  // open: C_out

  // Notes on the sheet:
  //   Attention, votre version de Logisim
  //   ne contient pas de tracker. Si vous
  //   enregistrez votre projet, toutes les
  //   informations du tracker seront
  //   définitivement effacées.
endmodule

module ADD1BIT (
  input  A,
  input  B,
  input  C_in,
  output D,
  output C_out
);

  wire and_1_out, and_2_out, and_3_out, xor_1_out;

  xor xor_1 (xor_1_out, A, B);
  and and_1 (and_1_out, A, B);
  and and_2 (and_2_out, A, C_in);
  and and_3 (and_3_out, B, C_in);
  or or_1 (C_out, and_1_out, and_2_out, and_3_out);
  xor xor_2 (D, xor_1_out, C_in);

  // Notes on the sheet:
  //   Attention, votre version de Logisim
  //   ne contient pas de tracker. Si vous
  //   enregistrez votre projet, toutes les
  //   informations du tracker seront
  //   définitivement effacées.
endmodule

module ADDSUB_ALU (
);


  // Notes on the sheet:
  //   Attention, votre version de Logisim
  //   ne contient pas de tracker. Si vous
  //   enregistrez votre projet, toutes les
  //   informations du tracker seront
  //   définitivement effacées.
endmodule

module ADD_SUB4BITS (
  input  Sub,
  input  [3:0] A,
  input  [3:0] B,
  output [3:0] D
);

  wire [3:0] xor_1_out;

  xor xor_1 (xor_1_out[0], Sub, A[0]);
  xor xor_2 (xor_1_out[1], Sub, A[1]);
  xor xor_3 (xor_1_out[2], Sub, A[2]);
  xor xor_4 (xor_1_out[3], Sub, A[3]);
  ADD4BITS add4bits_1 (.A(xor_1_out), .B(B), .C_in(Sub), .D(D));  // open: C_out

  // Notes on the sheet:
  //   Attention, votre version de Logisim
  //   ne contient pas de tracker. Si vous
  //   enregistrez votre projet, toutes les
  //   informations du tracker seront
  //   définitivement effacées.
endmodule

module ADD4BITS (
  input  [3:0] A,
  input  [3:0] B,
  input  C_in,
  output [3:0] D,
  output C_out
);

  wire add1bit_1_c_out, add1bit_2_c_out, add1bit_3_c_out;

  ADD1BIT add1bit_1 (.A(A[0]), .B(B[0]), .C_in(C_in), .D(D[0]), .C_out(add1bit_1_c_out));
  ADD1BIT add1bit_2 (.A(A[1]), .B(B[1]), .C_in(add1bit_1_c_out), .D(D[1]), .C_out(add1bit_2_c_out));
  ADD1BIT add1bit_3 (.A(A[2]), .B(B[2]), .C_in(add1bit_2_c_out), .D(D[2]), .C_out(add1bit_3_c_out));
  ADD1BIT add1bit_4 (.A(A[3]), .B(B[3]), .C_in(add1bit_3_c_out), .D(D[3]), .C_out(C_out));

  // Notes on the sheet:
  //   Attention, votre version de Logisim
  //   ne contient pas de tracker. Si vous
  //   enregistrez votre projet, toutes les
  //   informations du tracker seront
  //   définitivement effacées.
endmodule
